// Logisim project circuito.circ as structural Verilog: 1 circuit, main circuit main
module main (
  input  X
);

  wire and_1_out, and_2_out, and_3_out, and_4_out, clock_1_out, d_ff_1_q, d_ff_2_q, d_ff_2_qn, d_ff_3_q,
       d_ff_3_qn, or_1_out, or_2_out, or_3_out;

  and and_1 (and_1_out, ~X, or_1_out);  // AND_Gate
  or or_1 (or_1_out, d_ff_1_q, d_ff_3_q);
  and and_2 (and_2_out, d_ff_2_q, d_ff_3_qn, X);
  or or_2 (or_2_out, d_ff_3_qn, d_ff_2_qn);
  Clock clock_1 (.out(clock_1_out));
  and and_3 (and_3_out, d_ff_2_q, d_ff_3_q, X);
  or or_3 (or_3_out, and_1_out, and_2_out);
  and and_4 (and_4_out, X, or_2_out);
  D_Flip_Flop d_ff_1 (.clk(clock_1_out), .D(and_3_out), .Q(d_ff_1_q), .en(1'b1));  // open: Qn, preset, reset
  D_Flip_Flop d_ff_2 (.clk(clock_1_out), .D(or_3_out), .Q(d_ff_2_q), .Qn(d_ff_2_qn), .en(1'b1));  // open: preset, reset
  D_Flip_Flop d_ff_3 (
    .clk(clock_1_out), .D(and_4_out), .Q(d_ff_3_q), .Qn(d_ff_3_qn), .en(1'b1));  // open: preset, reset
  LED led_1 (.in(d_ff_1_q));

  // Notes on the sheet:
  //   CLOCK
  //   D-A
  //   D-B
  //   D-C
  //   ENABLE
  //   S
endmodule
